// Logisim project 8BIT_CPU.circ as structural Verilog: 5 circuits, main circuit main
module ALU (
  input  B3,
  input  Bo,
  input  A1,
  input  B1,
  input  B2,
  input  Ao,
  input  A2,
  input  A3,
  input  So,
  input  S1,
  input  S2,
  input  S3,
  input  Cn,
  input  M,
  output AequalsB,
  output P,
  output Cout,
  output F3,
  output F0,
  output F2,
  output F1
);

  wire and_1_out, and_2_out, and_3_out, and_4_out, and_5_out, and_6_out, and_7_out, and_8_out, and_9_out,
       and_10_out, and_12_out, and_13_out, and_14_out, and_15_out, and_16_out, and_17_out, and_18_out,
       and_19_out, and_20_out, and_21_out, and_22_out, and_23_out, and_24_out, and_25_out, and_26_out,
       and_27_out, and_28_out, and_29_out, and_30_out, and_31_out, and_32_out, and_33_out, buffer_1_out,
       buffer_2_out, buffer_3_out, buffer_4_out, buffer_5_out, nand_1_out, nand_3_out, nor_1_out, nor_2_out,
       nor_3_out, nor_4_out, nor_5_out, nor_6_out, nor_7_out, nor_8_out, nor_9_out, nor_10_out, nor_11_out,
       nor_12_out, not_1_out, not_2_out, not_3_out, not_5_out, not_6_out, not_8_out, not_9_out, not_10_out,
       not_11_out, not_13_out, not_14_out, not_15_out, not_16_out, not_18_out, not_19_out, not_20_out,
       not_21_out, not_22_out, not_23_out, xor_1_out, xor_2_out, xor_3_out, xor_4_out;

  not not_1 (not_1_out, Ao);
  buf buffer_1 (buffer_1_out, not_1_out);
  not not_2 (not_2_out, M);
  not not_3 (not_3_out, nor_1_out);
  nand nand_1 (nand_1_out, Cn, not_2_out);
  xor xor_1 (xor_1_out, nand_1_out, and_2_out);
  not not_4 (F0, xor_1_out);
  and and_1 (and_1_out, not_5_out, So);
  nor nor_1 (nor_1_out, buffer_1_out, and_1_out, and_3_out);
  and and_2 (and_2_out, not_3_out, nor_2_out);
  and and_3 (and_3_out, S1, not_6_out);
  not not_5 (not_5_out, Bo);
  not not_6 (not_6_out, not_5_out);
  and and_4 (and_4_out, not_6_out, S2, not_1_out);
  and and_5 (and_5_out, not_2_out, nor_1_out);
  and and_6 (and_6_out, not_1_out, S3, not_5_out);
  nor nor_2 (nor_2_out, and_4_out, and_6_out);
  and and_7 (and_7_out, not_2_out, nor_2_out, Cn);
  nor nor_3 (nor_3_out, and_5_out, and_7_out);
  xor xor_2 (xor_2_out, nor_3_out, and_8_out);
  not not_7 (F1, xor_2_out);
  not not_8 (not_8_out, nor_4_out);
  and and_8 (and_8_out, not_8_out, nor_6_out);
  not not_9 (not_9_out, A1);
  buf buffer_2 (buffer_2_out, not_9_out);
  and and_9 (and_9_out, not_10_out, So);
  nor nor_4 (nor_4_out, buffer_2_out, and_9_out, and_12_out);
  and and_10 (and_10_out, not_2_out, nor_4_out);
  and and_11 (AequalsB, xor_1_out, xor_2_out, xor_3_out, xor_4_out);
  not not_10 (not_10_out, B1);
  not not_11 (not_11_out, not_10_out);
  and and_12 (and_12_out, S1, not_11_out);
  and and_13 (and_13_out, not_2_out, nor_1_out, nor_6_out);
  nor nor_5 (nor_5_out, and_10_out, and_13_out, and_15_out);
  and and_14 (and_14_out, not_11_out, S2, not_9_out);
  nor nor_6 (nor_6_out, and_14_out, and_16_out);
  and and_15 (and_15_out, not_2_out, Cn, nor_2_out, nor_6_out);
  xor xor_3 (xor_3_out, nor_5_out, and_17_out);
  not not_12 (F2, xor_3_out);
  and and_16 (and_16_out, not_9_out, S3, not_10_out);
  not not_13 (not_13_out, nor_7_out);
  and and_17 (and_17_out, not_13_out, nor_9_out);
  not not_14 (not_14_out, A2);
  buf buffer_3 (buffer_3_out, not_14_out);
  and and_18 (and_18_out, not_15_out, So);
  nor nor_7 (nor_7_out, buffer_3_out, and_18_out, and_20_out);
  and and_19 (and_19_out, not_2_out, nor_7_out);
  and and_20 (and_20_out, S1, not_16_out);
  and and_21 (and_21_out, not_2_out, nor_4_out, nor_9_out);
  nor nor_8 (nor_8_out, and_19_out, and_21_out, and_23_out, and_25_out);
  not not_15 (not_15_out, B2);
  not not_16 (not_16_out, not_15_out);
  and and_22 (and_22_out, not_16_out, S2, not_14_out);
  and and_23 (and_23_out, not_2_out, nor_1_out, nor_6_out, nor_9_out);
  xor xor_4 (xor_4_out, nor_8_out, and_26_out);
  not not_17 (F3, xor_4_out);
  and and_24 (and_24_out, not_14_out, S3, not_15_out);
  nor nor_9 (nor_9_out, and_22_out, and_24_out);
  and and_25 (and_25_out, not_2_out, Cn, nor_2_out, nor_6_out, nor_9_out);
  not not_18 (not_18_out, nor_10_out);
  and and_26 (and_26_out, not_18_out, nor_11_out);
  not not_19 (not_19_out, A3);
  buf buffer_4 (buffer_4_out, not_19_out);
  and and_27 (and_27_out, not_20_out, So);
  nor nor_10 (nor_10_out, buffer_4_out, and_27_out, and_28_out);
  nand nand_2 (P, nor_2_out, nor_6_out, nor_9_out, nor_11_out);
  not not_20 (not_20_out, B3);
  not not_21 (not_21_out, not_20_out);
  and and_28 (and_28_out, S1, not_21_out);
  nand nand_3 (nand_3_out, Cn, nor_2_out, nor_6_out, nor_9_out, nor_11_out);
  and and_29 (and_29_out, not_21_out, S2, not_19_out);
  and and_30 (and_30_out, nor_1_out, nor_6_out, nor_9_out, nor_11_out);
  not not_22 (not_22_out, nand_3_out);
  not not_23 (not_23_out, nor_12_out);
  or or_1 (Cout, not_22_out, not_23_out);
  and and_31 (and_31_out, not_19_out, S3, not_20_out);
  nor nor_11 (nor_11_out, and_29_out, and_31_out);
  and and_32 (and_32_out, nor_4_out, nor_9_out, nor_11_out);
  nor nor_12 (nor_12_out, and_30_out, and_32_out, and_33_out, buffer_5_out);
  and and_33 (and_33_out, nor_7_out, nor_11_out);
  buf buffer_5 (buffer_5_out, nor_10_out);
endmodule

module main (
  input  in_1,
  input  in_2,
  input  in_3,
  input  in_4,
  input  [7:0] in_5,
  input  in_6,
  input  in_7,
  input  in_8,
  input  in_9,
  output [7:0] out_10,
  output [7:0] out_11,
  output [1:0] out_12,
  output [7:0] out_13,
  output [7:0] out_14,
  output [1:0] out_15,
  output [7:0] out_16,
  output [1:0] out_17,
  output [7:0] out_18,
  output [1:0] out_19,
  output [1:0] out_20,
  output [1:0] out_21,
  output [1:0] out_22,
  output [5:0] out_23,
  output [1:0] out_24,
  output [1:0] out_25,
  output [7:0] out_26,
  output [7:0] out_27,
  output [7:0] out_28,
  output [7:0] out_29,
  output [7:0] out_30,
  output [7:0] out_31
);

  wire AequalsB_q, AequalsB_qn, and_1_out, and_2_out, and_3_out, and_4_out, and_5_out, and_6_out, and_7_out,
       and_8_out, clock1_1_primary_clock, clock1_1_secondary_clock, demultiplexer_1_out0,
       demultiplexer_1_out1, demultiplexer_1_out2, demultiplexer_1_out3, demultiplexer_4_out0,
       eightbitalu_1_aequalsb, eightbitalu_1_cout, not_1_out, or_1_out, sign_q, sign_qn;
  wire [1:0] pla_1_out;
  wire [4:0] button_1_out, JUMP_st_out;
  wire [6:0] ALU_MS_p2, multiplexer_3_out;
  wire [7:0] counter_2_q, demultiplexer_2_out0, demultiplexer_2_out1, demultiplexer_3_out1,
       demultiplexer_5_out0, demultiplexer_5_out1, demultiplexer_6_out0, demultiplexer_6_out1, display_1_d0,
       display_1_d1, display_1_d2, display_1_d3, display_1_d4, display_1_d5, display_1_d6, display_1_d7,
       display_1_d8, display_1_d9, eightbitalu_1_f0, Memory_Columb_select_dout, multiplexer_4_out, R0_q,
       R1_q, R2_q, R3_q;
  wire [11:0] CU_p2;

  Multiplexer #(.select(2), .width(8)) multiplexer_1 (
    .in0(R0_q), .in1(R1_q), .in2(R2_q), .in3(R3_q), .out(out_28), .sel(out_23[1:0]));
  Multiplexer #(.select(2), .width(8)) multiplexer_2 (
    .in0(R0_q), .in1(R1_q), .in2(R2_q), .in3(R3_q), .out(out_29), .sel(out_15));
  Register #(.trigger("high")) R0 (
    .D(out_11), .en(demultiplexer_1_out0), .clk(demultiplexer_1_out0), .Q(R0_q));  // open: clr
  Register #(.trigger("high")) R1 (
    .D(out_11), .en(demultiplexer_1_out1), .clk(demultiplexer_1_out1), .Q(R1_q));  // open: clr
  and and_1 (and_1_out, multiplexer_3_out[6], clock1_1_secondary_clock);
  Register #(.trigger("high")) Accumulater (
    .D(eightbitalu_1_f0), .en(and_1_out), .clk(and_1_out), .Q(out_10));  // open: clr
  Register #(.trigger("high")) R2 (
    .D(out_11), .en(demultiplexer_1_out2), .clk(demultiplexer_1_out2), .Q(R2_q));  // open: clr
  RAM #(.addrWidth(4), .trigger("high")) Arr ();  // open: addr, we, oe, clk, din, dout
  EightBitALU eightbitalu_1 (
    .A0(out_28[0]), .B0(out_29[0]), .B1(out_29[1]), .B2(out_29[2]), .B3(out_29[3]), .B4(out_29[4]),
    .B5(out_29[5]), .B6(out_29[6]), .B7(out_29[7]), .A1(out_28[1]), .A2(out_28[2]), .A3(out_28[3]),
    .A4(out_28[4]), .A5(out_28[5]), .A6(out_28[6]), .A7(out_28[7]), .M(multiplexer_3_out[0]),
    .Cn(multiplexer_3_out[1]), .S3(multiplexer_3_out[2]), .S2(multiplexer_3_out[3]),
    .S1(multiplexer_3_out[4]), .S0(multiplexer_3_out[5]), .AequalsB(eightbitalu_1_aequalsb),
    .Cout(eightbitalu_1_cout), .F4(eightbitalu_1_f0[4]), .F1(eightbitalu_1_f0[1]), .F0(eightbitalu_1_f0[0]),
    .F5(eightbitalu_1_f0[5]), .F6(eightbitalu_1_f0[6]), .F7(eightbitalu_1_f0[7]), .F2(eightbitalu_1_f0[2]),
    .F3(eightbitalu_1_f0[3]));
  // PlaRom #(.Contents("1*3 2 1 1 2 1 2 1 1 2 2 1 2 1 2 1*3 2 1 2*4 1 2 1 2 2 1 1 1 0 0 1 0 0 1 0 1 1 0 1 0 1 0 1*3 0 1*4 0 1 0 1 1 0*5 1*3 0 0 1 0 1*7 0 1 0*6"), .\and (8), .outputs(7)) ALU_MS: pin names not known; wires that end beside it: out_23[5:2], ALU_MS_p2
  Register #(.trigger("high")) R3 (
    .D(out_11), .en(demultiplexer_1_out3), .clk(demultiplexer_1_out3), .Q(R3_q));  // open: clr
  not not_1 (not_1_out, in_9);
  Multiplexer #(.width(7)) multiplexer_3 (
    .in0({out_23[4:0], out_15}), .in1(ALU_MS_p2), .out(multiplexer_3_out), .sel(not_1_out));
  and and_2 (and_2_out, multiplexer_3_out[6], clock1_1_secondary_clock);
  Multiplexer #(.select(2), .width(8)) multiplexer_4 (
    .in0(R0_q), .in1(R1_q), .in2(R2_q), .in3(R3_q), .out(multiplexer_4_out), .sel(out_21));
  PLA #(.in_width(8), .out_width(5), .\table ("01110000 00001 # Jump to address\n01110001 00000\n01110010 00000\n01110011 00000\n01110100 10000 # jump if negative")) JUMP_st (
    .in({out_23, out_15}), .out(JUMP_st_out));
  D_Flip_Flop AequalsB (
    .D(eightbitalu_1_aequalsb), .clk(and_2_out), .Q(AequalsB_q), .Qn(AequalsB_qn));  // open: preset, reset
  D_Flip_Flop sign (.D(eightbitalu_1_cout), .clk(and_2_out), .Q(sign_q), .Qn(sign_qn));  // open: preset, reset
  Demultiplexer #(.select(2)) demultiplexer_1 (
    .out0(demultiplexer_1_out0), .out1(demultiplexer_1_out1), .out2(demultiplexer_1_out2),
    .out3(demultiplexer_1_out3), .in(and_3_out), .sel(out_15));
  and and_3 (and_3_out, CU_p2[11], clock1_1_secondary_clock);
  Counter counter_1 (.load(in_1), .up(in_2), .count(in_3), .clk(in_4), .D(in_5));  // open: clr, carry, Q
  // PlaRom #(.Contents("1 2 1*5 2 1*3 2*3 1*4 2 2 1*3 2*3 1 1 2 1 2 2 1 1 2*5 1 0 0 2*3 1 0 2*4 1 2 1 2*3 1 2 2 1 1 2 2 1*4 2 2 1 2 1 1 2*3 1*8 2 1 2 1*3 2 1 2 1 2 1 2 1 2 2 1 1 2 1 2*3 0 0 1 0 0 1 0*4 1 0*5 1 0 1 0 1 0*3 1 1 0*5 1 1 0 1 0*3 1 0 1 1 0 1 0 1 1 0 1 0*3 1 0 1*3 0 0 1 1 0 1 0*3 1 0 1*4 0 1 1 0 1 0*3 1 0 1 1 0 0 1 0 1*3 0 1 0 1 1 0*3 1 1 0 1*3 0 1 0 1 1 0 0 1 0 1 0 1*3 0 1 0 1 1 0 0 1*3 0 1*3 0 1 0 1 1 0*4 1 1 0 1*6 0*5 1 0 1*4 0 0 1 1 0*5 1 1 0 1 0 0 1 0 0 1 0*4 1*4 0 1*4 0*5 1*5 0 0 1 0 1 1 0 1 0 1*5 0 0 1 0 1*3 0 0 1*5 0 0 1 0 1*4 0 1*5 0 0 1 0 1 1"), .\and (18), .outputs(14)) CU: pin names not known; wires that end beside it: out_23, {out_21, CU_p2[11], out_12, out_22, out_17, out_19, CU_p2[2:0]}
  CLOCK1 clock1_1 (.Primary_clock(clock1_1_primary_clock), .Secondary_clock(clock1_1_secondary_clock));
  and and_4 (and_4_out, JUMP_st_out[1], AequalsB_q);
  and and_5 (and_5_out, JUMP_st_out[2], AequalsB_qn);
  and and_6 (and_6_out, JUMP_st_out[3], sign_q);
  and and_7 (and_7_out, JUMP_st_out[4], sign_qn);
  Demultiplexer #(.width(8)) demultiplexer_2 (
    .out0(demultiplexer_2_out0), .out1(demultiplexer_2_out1), .in(multiplexer_4_out), .sel(CU_p2[0]));
  or or_1 (or_1_out, JUMP_st_out[0], and_4_out, and_5_out, and_6_out, and_7_out);
  Multiplexer #(.select(2), .width(8)) multiplexer_5 (
    .in0(demultiplexer_6_out1), .in1(demultiplexer_2_out0), .in2(out_10), .out(out_13), .sel(out_17));  // open: in3
  and and_8 (and_8_out, CU_p2[1], clock1_1_secondary_clock);
  Counter counter_2 (
    .clr(in_7), .load(or_1_out), .up(in_8), .count(demultiplexer_4_out0), .clk(clock1_1_primary_clock),
    .D(out_27), .Q(counter_2_q));  // open: carry
  Demultiplexer #(.width(8)) demultiplexer_3 (
    .out1(demultiplexer_3_out1), .in(out_13), .sel(pla_1_out[0]));  // open: out0
  RAM #(.trigger("high")) Memory_Columb_select (
    .addr(out_13), .we(and_8_out), .oe(CU_p2[2]), .din(out_18), .dout(Memory_Columb_select_dout));
  Multiplexer #(.select(2), .width(8)) multiplexer_6 (
    .in0(demultiplexer_6_out0), .in1(demultiplexer_2_out1), .in2(out_10), .out(out_18), .sel(out_19));  // open: in3
  Demultiplexer demultiplexer_4 (.out0(demultiplexer_4_out0), .in(in_6), .sel(pla_1_out[1]));  // open: out1
  ROM rom_1 (.addr(counter_2_q), .data({out_23, out_15}));
  Multiplexer #(.select(2), .width(8)) multiplexer_7 (
    .in0(out_16), .in1(demultiplexer_5_out0), .in2(out_10), .out(out_11), .sel(out_12));  // open: in3
  PLA #(.in_width(8), .\table ("00000000 01 # ii\n11111111 10")) pla_1 (.in({out_23, out_15}), .out(pla_1_out));
  Demultiplexer #(.width(8)) demultiplexer_5 (
    .out0(demultiplexer_5_out0), .out1(demultiplexer_5_out1), .in(Memory_Columb_select_dout),
    .sel(pla_1_out[0]));
  ROM rom_2 (.addr(counter_2_q), .data(out_27));
  Demultiplexer #(.select(2), .width(8)) demultiplexer_6 (
    .out0(demultiplexer_6_out0), .out1(demultiplexer_6_out1), .out2(out_16), .in(out_27), .sel(out_22));  // open: out3
  Display display_1 (
    .Addressin(demultiplexer_3_out1), .DATAin(demultiplexer_5_out1), .Update(clock1_1_secondary_clock),
    .D0(display_1_d0), .D1(display_1_d1), .D2(display_1_d2), .D3(display_1_d3), .D4(display_1_d4),
    .D5(display_1_d5), .D6(display_1_d6), .D7(display_1_d7), .D8(display_1_d8), .D9(display_1_d9));
  DotMatrix #(.inputtype("row"), .matrixcols(8), .matrixrows(10)) dotmatrix_1 (
    .row0(display_1_d0), .row1(display_1_d1), .row2(display_1_d2), .row3(display_1_d3), .row4(display_1_d4),
    .row5(display_1_d5), .row6(display_1_d6), .row7(display_1_d7), .row8(display_1_d8), .row9(display_1_d9));
  Button button_1 (.out(button_1_out[0]));
  Button button_2 (.out(button_1_out[1]));
  Button button_3 (.out(button_1_out[3]));
  Button button_4 (.out(button_1_out[2]));
  Button button_5 (.out(button_1_out[4]));

  assign out_14 = out_11;
  assign out_20 = out_15;
  assign out_24 = out_23[1:0];
  assign out_25 = out_22;
  assign out_26 = {out_23, out_15};
  assign out_30 = out_27;
  assign out_31 = out_10;

  // Notes on the sheet:
  //   contents of rom_1 (hex, n*v repeats v):
  //   c0 e2 c8 d0 30 e3 ab 32 44 60 30 e3 ab 32 40 11 30 58 45 60 54 40 41 0 d0 30 24 74 70 ff a1 105*0 70
  //   16*0 50
  //   contents of rom_2 (hex, n*v repeats v):
  //   1c 0 1d 5*0 1c 5*0 7 0 0 0 1d 0 0 8 11 0 0 11 0 1d 17
endmodule

module Display (
  input  [7:0] Addressin,
  input  [7:0] DATAin,
  input  Update,
  output [7:0] D0,
  output [7:0] D1,
  output [7:0] D2,
  output [7:0] D3,
  output [7:0] D4,
  output [7:0] D5,
  output [7:0] D6,
  output [7:0] D7,
  output [7:0] D8,
  output [7:0] D9
);

  wire [9:0] pla_1_out;

  PLA #(.in_width(8), .out_width(10), .\table ("00001000 0000000001 # 1\n00001001 0000000010 # 2\n00001010 0000000100 # 3\n00001011 0000001000 # 4\n00001100 0000010000 # 5\n00001101 0000100000 # 6\n00001110 0001000000 # 7\n00001111 0010000000 # 8\n00010000 0100000000 # 9\n00010001 1000000000 # 10")) pla_1 (
    .in(Addressin), .out(pla_1_out));
  Register #(.trigger("high")) register_1 (.D(DATAin), .en(pla_1_out[0]), .clk(Update), .Q(D0));  // open: clr
  Register #(.trigger("high")) register_2 (.D(DATAin), .en(pla_1_out[1]), .clk(Update), .Q(D1));  // open: clr
  Register #(.trigger("high")) register_3 (.D(DATAin), .en(pla_1_out[2]), .clk(Update), .Q(D2));  // open: clr
  Register #(.trigger("high")) register_4 (.D(DATAin), .en(pla_1_out[3]), .clk(Update), .Q(D3));  // open: clr
  Register #(.trigger("high")) register_5 (.D(DATAin), .en(pla_1_out[4]), .clk(Update), .Q(D4));  // open: clr
  Register #(.trigger("high")) register_6 (.D(DATAin), .en(pla_1_out[5]), .clk(Update), .Q(D5));  // open: clr
  Register #(.trigger("high")) register_7 (.D(DATAin), .en(pla_1_out[6]), .clk(Update), .Q(D6));  // open: clr
  Register #(.trigger("high")) register_8 (.D(DATAin), .en(pla_1_out[7]), .clk(Update), .Q(D7));  // open: clr
  Register #(.trigger("high")) register_9 (.D(DATAin), .en(pla_1_out[8]), .clk(Update), .Q(D8));  // open: clr
  Register #(.trigger("high")) register_10 (.D(DATAin), .en(pla_1_out[9]), .clk(Update), .Q(D9));  // open: clr
endmodule

module CLOCK1 (
  output Primary_clock,
  output Secondary_clock
);

  Clock #(.highDuration(3)) clock_1 (.out(Primary_clock));
  Clock #(.lowDuration(3), .phaseOffset(1)) clock_2 (.out(Secondary_clock));
endmodule

module EightBitALU (
  input  A0,
  input  B0,
  input  B1,
  input  B2,
  input  B3,
  input  B4,
  input  B5,
  input  B6,
  input  B7,
  input  A1,
  input  A2,
  input  A3,
  input  A4,
  input  A5,
  input  A6,
  input  A7,
  input  M,
  input  Cn,
  input  S3,
  input  S2,
  input  S1,
  input  S0,
  output AequalsB,
  output Cout,
  output F4,
  output F1,
  output F0,
  output F5,
  output F6,
  output F7,
  output F2,
  output F3
);

  wire alu_1_aequalsb, alu_1_cout, alu_2_aequalsb;

  ALU alu_1 (
    .B3(B3), .Bo(B0), .A1(A1), .B1(B1), .B2(B2), .Ao(A0), .A2(A2), .A3(A3), .So(S0), .S1(S1), .S2(S2),
    .S3(S3), .Cn(Cn), .M(M), .AequalsB(alu_1_aequalsb), .Cout(alu_1_cout), .F3(F3), .F0(F0), .F2(F2), .F1(F1));  // open: P
  ALU alu_2 (
    .B3(B7), .Bo(B4), .A1(A5), .B1(B5), .B2(B6), .Ao(A4), .A2(A6), .A3(A7), .So(S0), .S1(S1), .S2(S2),
    .S3(S3), .Cn(alu_1_cout), .M(M), .AequalsB(alu_2_aequalsb), .Cout(Cout), .F3(F7), .F0(F4), .F2(F6),
    .F1(F5));  // open: P
  and and_1 (AequalsB, alu_1_aequalsb, alu_2_aequalsb);
endmodule
